// Logisim project add_16b.circ as structural Verilog: 6 circuits, main circuit main
module main (
);

  additionneur_16b additionneur_16b_1 ();  // open: a15, a14, a13, a12, a11, a10, a9, a8, a7, a6, a5, a4, a3, a2, a1, a0, b15, b14, b13, b12, b11, b10, b9, b8, b7, b6, b5, b4, b3, b2, b1, b0, c0, s16, s15, s14, s13, s12, s11, s10, s9, s8, s7, s6, s5, s4, s3, s2, s1, s0
endmodule

module add (
  input  C,
  input  A,
  input  B,
  output S,
  output P,
  output G
);

  wire xor_1_out;

  or or_1 (P, A, B);
  and and_1 (G, A, B);
  xor xor_1 (xor_1_out, A, B);
  xor xor_2 (S, C, xor_1_out);
endmodule

module unite_de_calcul_4b (
  input  g3,
  input  p3,
  input  g2,
  input  p2,
  input  g1,
  input  p1,
  input  g0,
  input  p0,
  input  c0,
  output sp,
  output c3,
  output c4,
  output c2,
  output c1,
  output sg
);

  wire and_1_out, and_2_out, and_3_out, and_4_out, and_5_out, and_6_out, and_7_out, and_8_out, and_9_out,
       and_10_out, and_12_out, and_13_out, and_14_out;

  and and_1 (and_1_out, p2, g1, p3);
  and and_2 (and_2_out, p2, p1, g0, p3);
  and and_3 (and_3_out, p2, p1, c0, p3);
  or or_1 (c4, g3, and_1_out, and_2_out, and_3_out, and_4_out);
  and and_4 (and_4_out, p3, g2);
  and and_5 (and_5_out, p2, p1, g0);
  and and_6 (and_6_out, p2, p1, p0, c0);
  or or_2 (c3, g2, and_5_out, and_6_out, and_7_out);
  and and_7 (and_7_out, p2, g1);
  and and_8 (and_8_out, p1, c0, p0);
  and and_9 (and_9_out, g0, p1);
  or or_3 (c2, and_8_out, g1, and_9_out);
  or or_4 (c1, g0, and_10_out);
  and and_10 (and_10_out, p0, c0);
  and and_11 (sp, p3, p2, p1, p0);
  and and_12 (and_12_out, g2, p3);
  and and_13 (and_13_out, g1, p2, p3);
  or or_5 (sg, g3, and_12_out, and_13_out, and_14_out);
  and and_14 (and_14_out, g0, p1, p2, p3);
endmodule

module add_4b (
  input  B4,
  input  B3,
  input  B2,
  input  B1,
  input  A4,
  input  A3,
  input  A2,
  input  A1,
  input  C0,
  output S5,
  output S4,
  output S3,
  output S2,
  output S1,
  output sg,
  output sp
);

  wire add_1_g, add_1_p, add_2_g, add_2_p, add_3_g, add_3_p, add_4_g, add_4_p, unite_de_calcul_4b_1_c1,
       unite_de_calcul_4b_1_c2, unite_de_calcul_4b_1_c3;

  add add_1 (.C(C0), .A(A1), .B(B1), .S(S1), .P(add_1_p), .G(add_1_g));
  add add_2 (.C(unite_de_calcul_4b_1_c1), .A(A2), .B(B2), .S(S2), .P(add_2_p), .G(add_2_g));
  add add_3 (.C(unite_de_calcul_4b_1_c2), .A(A3), .B(B3), .S(S3), .P(add_3_p), .G(add_3_g));
  add add_4 (.C(unite_de_calcul_4b_1_c3), .A(A4), .B(B4), .S(S4), .P(add_4_p), .G(add_4_g));
  unite_de_calcul_4b unite_de_calcul_4b_1 (
    .g3(add_4_g), .p3(add_4_p), .g2(add_3_g), .p2(add_3_p), .g1(add_2_g), .p1(add_2_p), .g0(add_1_g),
    .p0(add_1_p), .c0(C0), .sp(sp), .c3(unite_de_calcul_4b_1_c3), .c4(S5), .c2(unite_de_calcul_4b_1_c2),
    .c1(unite_de_calcul_4b_1_c1), .sg(sg));
endmodule

module unite_calcul_16b (
  input  sg3,
  input  sp3,
  input  sg2,
  input  sp2,
  input  sg1,
  input  sp1,
  input  sg0,
  input  sp0,
  input  c0,
  output c3,
  output c4,
  output c2,
  output c1
);

  wire and_1_out, and_2_out, and_3_out, and_4_out, and_5_out, and_6_out, and_7_out, and_8_out, and_9_out,
       and_10_out;

  and and_1 (and_1_out, sp2, sg1, sp3);
  and and_2 (and_2_out, sp2, sp1, sg0, sp3);
  and and_3 (and_3_out, sp2, sp1, c0, sp3);
  or or_1 (c4, sg3, and_1_out, and_2_out, and_3_out, and_4_out);
  and and_4 (and_4_out, sp3, sg2);
  and and_5 (and_5_out, sp2, sp1, sg0);
  and and_6 (and_6_out, sp2, sp1, sp0, c0);
  or or_2 (c3, sg2, and_5_out, and_6_out, and_7_out);
  and and_7 (and_7_out, sp2, sg1);
  and and_8 (and_8_out, sp1, c0, sp0);
  and and_9 (and_9_out, sg0, sp1);
  or or_3 (c2, and_8_out, sg1, and_9_out);
  or or_4 (c1, sg0, and_10_out);
  and and_10 (and_10_out, sp0, c0);
endmodule

module additionneur_16b (
  input  a15,
  input  a14,
  input  a13,
  input  a12,
  input  a11,
  input  a10,
  input  a9,
  input  a8,
  input  a7,
  input  a6,
  input  a5,
  input  a4,
  input  a3,
  input  a2,
  input  a1,
  input  a0,
  input  b15,
  input  b14,
  input  b13,
  input  b12,
  input  b11,
  input  b10,
  input  b9,
  input  b8,
  input  b7,
  input  b6,
  input  b5,
  input  b4,
  input  b3,
  input  b2,
  input  b1,
  input  b0,
  input  c0,
  output s16,
  output s15,
  output s14,
  output s13,
  output s12,
  output s11,
  output s10,
  output s9,
  output s8,
  output s7,
  output s6,
  output s5,
  output s4,
  output s3,
  output s2,
  output s1,
  output s0
);

  wire add_4b_1_sg, add_4b_1_sp, add_4b_2_sg, add_4b_2_sp, add_4b_3_sg, add_4b_3_sp, add_4b_4_sg,
       add_4b_4_sp, unite_calcul_16b_1_c1, unite_calcul_16b_1_c2, unite_calcul_16b_1_c3;

  add_4b add_4b_1 (
    .B4(b3), .B3(b2), .B2(b1), .B1(b0), .A4(a3), .A3(a2), .A2(a1), .A1(a0), .C0(c0), .S4(s3), .S3(s2),
    .S2(s1), .S1(s0), .sg(add_4b_1_sg), .sp(add_4b_1_sp));  // open: S5
  add_4b add_4b_2 (
    .B4(b7), .B3(b6), .B2(b5), .B1(b4), .A4(a7), .A3(a6), .A2(a5), .A1(a4), .C0(unite_calcul_16b_1_c1),
    .S4(s7), .S3(s6), .S2(s5), .S1(s4), .sg(add_4b_2_sg), .sp(add_4b_2_sp));  // open: S5
  add_4b add_4b_3 (
    .B4(b11), .B3(b10), .B2(b9), .B1(b8), .A4(a11), .A3(a10), .A2(a9), .A1(a8), .C0(unite_calcul_16b_1_c2),
    .S4(s11), .S3(s10), .S2(s9), .S1(s8), .sg(add_4b_3_sg), .sp(add_4b_3_sp));  // open: S5
  add_4b add_4b_4 (
    .B4(b15), .B3(b14), .B2(b13), .B1(b12), .A4(a15), .A3(a14), .A2(a13), .A1(a12),
    .C0(unite_calcul_16b_1_c3), .S4(s15), .S3(s14), .S2(s13), .S1(s12), .sg(add_4b_4_sg), .sp(add_4b_4_sp));  // open: S5
  unite_calcul_16b unite_calcul_16b_1 (
    .sg3(add_4b_4_sg), .sp3(add_4b_4_sp), .sg2(add_4b_3_sg), .sp2(add_4b_3_sp), .sg1(add_4b_2_sg),
    .sp1(add_4b_2_sp), .sg0(add_4b_1_sg), .sp0(add_4b_1_sp), .c0(c0), .c3(unite_calcul_16b_1_c3), .c4(s16),
    .c2(unite_calcul_16b_1_c2), .c1(unite_calcul_16b_1_c1));
endmodule
