// Logisim project tp2.circ as structural Verilog
module add (
  input  C,
  input  A,
  input  B,
  output S,
  output P,
  output G
);

  wire xor_1_out;

  or or_1 (P, A, B);
  and and_1 (G, A, B);
  xor xor_1 (xor_1_out, A, B);
  xor xor_2 (S, C, xor_1_out);
endmodule

module unite_de_calcul (
  input  G3,
  input  P3,
  input  G2,
  input  P2,
  input  G1,
  input  P1,
  input  G0,
  input  P0,
  input  C0,
  output C4,
  output C3,
  output C2,
  output C1
);

  wire and_1_out, and_2_out, and_3_out, and_4_out;

  and and_1 (and_1_out, P3, C3);
  or or_1 (C4, G3, and_1_out);
  and and_2 (and_2_out, P2, C2);
  or or_2 (C3, G2, and_2_out);
  or or_3 (C2, G1, and_3_out);
  and and_3 (and_3_out, P1, C1);
  or or_4 (C1, G0, and_4_out);
  and and_4 (and_4_out, P0, C0);
endmodule

module add_4b (
  input  B4,
  input  B3,
  input  B2,
  input  B1,
  input  A4,
  input  A3,
  input  A2,
  input  A1,
  input  C0,
  output S5,
  output S4,
  output S3,
  output S2,
  output S1
);

  wire add_1_g, add_1_p, add_2_g, add_2_p, add_3_g, add_3_p, add_4_g, add_4_p, unite_de_calcul_1_c1,
       unite_de_calcul_1_c2, unite_de_calcul_1_c3;

  add add_1 (.C(C0), .A(A1), .B(B1), .S(S1), .P(add_1_p), .G(add_1_g));
  add add_2 (.C(unite_de_calcul_1_c1), .A(A2), .B(B2), .S(S2), .P(add_2_p), .G(add_2_g));
  add add_3 (.C(unite_de_calcul_1_c2), .A(A3), .B(B3), .S(S3), .P(add_3_p), .G(add_3_g));
  add add_4 (.C(unite_de_calcul_1_c3), .A(A4), .B(B4), .S(S4), .P(add_4_p), .G(add_4_g));
  unite_de_calcul unite_de_calcul_1 (
    .G3(add_4_g), .P3(add_4_p), .G2(add_3_g), .P2(add_3_p), .G1(add_2_g), .P1(add_2_p), .G0(add_1_g),
    .P0(add_1_p), .C0(C0), .C4(S5), .C3(unite_de_calcul_1_c3), .C2(unite_de_calcul_1_c2),
    .C1(unite_de_calcul_1_c1));
endmodule
